// Logisim project 21bce197DE_innovative.circ as structural Verilog: 1 circuit, main circuit main
module main (
  input  _1___Right_Shift,
  input  in_2,
  input  in_3,
  input  in_4,
  input  INPUT,
  input  A,
  input  B,
  input  C,
  input  D,
  output out_10,
  output [3:0] out_11,
  output out_12,
  output out_13,
  output out_14
);

  Multiplexer multiplexer_1 (.in0(INPUT), .in1(C), .out(out_10), .sel(_1___Right_Shift), .en(in_2));
  Multiplexer multiplexer_2 (.in0(A), .in1(C), .out(out_10), .sel(_1___Right_Shift), .en(in_3));
  Multiplexer multiplexer_3 (.in0(D), .in1(C), .out(out_10), .sel(_1___Right_Shift), .en(in_4));
  Multiplexer multiplexer_4 (.in0(D), .in1(B), .out(out_11[1]), .sel(_1___Right_Shift), .en(in_2));
  Multiplexer multiplexer_5 (.in0(D), .in1(B), .out(out_11[1]), .sel(_1___Right_Shift), .en(in_3));
  Multiplexer multiplexer_6 (.in0(D), .in1(B), .out(out_11[1]), .sel(_1___Right_Shift), .en(in_4));
  Multiplexer multiplexer_7 (.in0(C), .in1(A), .out(out_11[2]), .sel(_1___Right_Shift), .en(in_2));
  Multiplexer multiplexer_8 (.in0(C), .in1(A), .out(out_11[2]), .sel(_1___Right_Shift), .en(in_3));
  Multiplexer multiplexer_9 (.in0(C), .in1(A), .out(out_11[2]), .sel(_1___Right_Shift), .en(in_4));
  Multiplexer multiplexer_10 (.in0(B), .in1(INPUT), .out(out_11[3]), .sel(_1___Right_Shift), .en(in_2));
  Multiplexer multiplexer_11 (.in0(B), .in1(D), .out(out_11[3]), .sel(_1___Right_Shift), .en(in_3));
  Multiplexer multiplexer_12 (.in0(B), .in1(INPUT), .out(out_11[3]), .sel(_1___Right_Shift), .en(in_4));

  assign out_11[0] = out_10;
  assign out_12 = out_11[1];
  assign out_13 = out_11[2];
  assign out_14 = out_11[3];

  // Notes on the sheet:
  //   0 - Left Shift
  //   100 - Logical Shift
  //   010 - Circular Shift
  //   001 - Arithmetic Shift
endmodule
